# Fritzing sketch schematics (saved by Fritzing 0.9.3b)

parts:
  Part1 = Arduino Uno (Rev3)
  Part2 = HX711 Weighing Sensor Module
  Part3 = Bluetooth HC-05 Macho

nets:
  N1: Part1.D8, Part2.VCC
  N2: Part1.D9_PWM, Part2.DO/RX
  N3: Part1.D10_PWM/SS, Part2.GND
  N4: Part1.D11_PWM/MOSI, Part2.CK/TX
  N5: Part1.D0/RX, Part3.RXD
  N6: Part1.D1/TX, Part3.TXD
  5V: Part1.5V, Part3.VCC
  GND: Part1.GND, Part3.GND
